# Fritzing sketch fishbox_circuit (saved by Fritzing 0.9.2b)
breadboards: 1

parts:
  Raspberry_Pi1 = Raspberry Pi 2
  J1 = Power Jack [package=power_jack_pth]
  LED1 = LEDs [package=fkit-led-1206]
  Q1 = Basic FET N-Channel [package="TO220 [THT]"]

nets:
  GND: Raspberry_Pi1.GND, J1.GND, Q1.source
  N1: Raspberry_Pi1.GPIO18, Q1.gate
  N2: J1.PWR, LED1.A
  N3: LED1.C, Q1.drain
